// Logisim project muldiv.circ as structural Verilog: 3 circuits, main circuit main
module main (
  input  [15:0] Operand_1__Multiplicand_or_Dividend,
  input  [15:0] Operand_2__Multiplier_and_Divisor,
  input  Mul,
  input  Div,
  output [31:0] Product,
  output M_Ready,
  output [15:0] Quotient,
  output [15:0] Remainder,
  output D_Ready
);

  wire Clock_out;

  _16_bit_Multiplication u_16_bit_multiplication_1 (
    .Multiplicand(Operand_1__Multiplicand_or_Dividend), .Multiplier(Operand_2__Multiplier_and_Divisor),
    .Mul(Mul), .Clock(Clock_out), .Product(Product), .M_Ready(M_Ready));
  _16_bit_Division u_16_bit_division_1 (
    .Dividend(Operand_1__Multiplicand_or_Dividend), .Divisor(Operand_2__Multiplier_and_Divisor),
    .division_instruction(Div), .Clock(Clock_out), .Quotient(Quotient), .Remainder(Remainder),
    .division_ready(D_Ready));
  Clock Clock (.out(Clock_out));
endmodule

module _16_bit_Multiplication (
  input  [15:0] Multiplicand,
  input  [15:0] Multiplier,
  input  Mul,
  input  Clock,
  output [31:0] Product,
  output M_Ready
);

  wire and_1_out, and_2_out, comparator_1_eq, comparator_1_gt, comparator_1_lt, not_1_out, not_4_out,
       or_1_out;
  wire [7:0] counter_1_q, rom_1_data;
  wire [15:0] adder_1_out, adder_2_out, multiplexer_1_out, multiplexer_2_out, not_2_out, not_3_out;
  wire [31:0] adder_3_out, adder_4_out, bit_extender_1_out, bit_extender_2_out, multiplexer_3_out,
       multiplexer_4_out, multiplexer_5_out, multiplexer_6_out, multiplexer_7_out, multiplexer_8_out,
       Multiplicand_q, Multiplier_q, Product_q, shifter_1_out, shifter_2_out;

  Counter #(.max('h3)) counter_1 (
    .Q(counter_1_q), .carry(M_Ready), .clk(and_1_out), .clr(not_1_out));  // open: load, D, count
  not not_1 (not_1_out, Mul);
  and and_1 (and_1_out, Mul, Clock);
  assign not_2_out = ~Multiplicand;  // NOT_Gate not_2, 16 bits wide
  assign not_3_out = ~Multiplier;  // NOT_Gate not_3, 16 bits wide
  Adder #(.width(16)) adder_1 (.a(not_2_out), .b(16'h1), .out(adder_1_out));  // open: cin, cout
  Adder #(.width(16)) adder_2 (.a(not_3_out), .b(16'h1), .out(adder_2_out));  // open: cin, cout
  ROM rom_1 (.addr(counter_1_q), .data(rom_1_data));  // open: sel
  Multiplexer #(.width(16)) multiplexer_1 (
    .in0(Multiplicand), .in1(adder_1_out), .out(multiplexer_1_out), .sel(Multiplicand[15]));  // open: en
  Multiplexer #(.width(16)) multiplexer_2 (
    .in0(Multiplier), .in1(adder_2_out), .out(multiplexer_2_out), .sel(Multiplier[15]));  // open: en
  assign bit_extender_1_out = {{16{1'b0}}, multiplexer_1_out};  // Bit_Extender bit_extender_1
  Multiplexer #(.width(32), .enable("false")) multiplexer_3 (
    .in0(bit_extender_1_out), .in1(multiplexer_6_out), .out(multiplexer_3_out), .sel(rom_1_data[0]));
  assign bit_extender_2_out = {{16{1'b0}}, multiplexer_2_out};  // Bit_Extender bit_extender_2
  Multiplexer #(.width(32)) multiplexer_4 (
    .in0(bit_extender_2_out), .in1(multiplexer_7_out), .out(multiplexer_4_out), .sel(rom_1_data[0]));  // open: en
  Register #(.width(32)) u_Multiplicand (
    .D(multiplexer_3_out), .en(rom_1_data[1]), .Q(Multiplicand_q), .clk(and_1_out), .clr(not_4_out));
  Register #(.width(32)) u_Multiplier (
    .D(multiplexer_4_out), .en(rom_1_data[2]), .Q(Multiplier_q), .clk(and_1_out), .clr(not_4_out));
  not not_4 (not_4_out, Mul);
  Multiplier #(.width(32)) multiplier_2 (
    .a(bit_extender_1_out), .b(bit_extender_2_out), .out(Product));  // open: cin, cout
  Comparator #(.width(32)) comparator_1 (
    .a(Multiplicand_q), .b({32{1'b0}}), .gt(comparator_1_gt), .eq(comparator_1_eq), .lt(comparator_1_lt));
  Shifter #(.width(32)) shifter_1 (.in(Multiplicand_q), .\dist (5'b00001), .out(shifter_1_out));
  Shifter #(.width(32), .shift("lr")) shifter_2 (.in(Multiplier_q), .\dist (5'b00001), .out(shifter_2_out));
  or or_1 (or_1_out, comparator_1_gt, comparator_1_eq);
  and and_2 (and_2_out, or_1_out, rom_1_data[2]);
  Multiplexer #(.width(32)) multiplexer_5 (
    .in1(adder_3_out), .out(multiplexer_5_out), .sel(comparator_1_lt));  // open: in0, en
  Adder #(.width(32)) adder_3 (.a(shifter_1_out), .b(Product_q), .out(adder_3_out));  // open: cin, cout
  Multiplexer #(.width(32)) multiplexer_6 (
    .in0(multiplexer_5_out), .in1(Multiplicand_q), .out(multiplexer_6_out), .sel(and_2_out));  // open: en
  Multiplexer #(.width(32)) multiplexer_7 (
    .in0(Multiplier_q), .in1(shifter_2_out), .out(multiplexer_7_out), .sel(rom_1_data[4]));  // open: en
  Multiplexer #(.width(32), .enable("false")) multiplexer_8 (
    .in0(adder_4_out), .in1(Product_q), .out(multiplexer_8_out), .sel(comparator_1_lt));
  Register #(.width(32)) u_Product (
    .D(multiplexer_8_out), .en(rom_1_data[3]), .Q(Product_q), .clk(and_1_out), .clr(not_4_out));
  Shifter #(.width(32)) shifter_3 (.in(Product_q), .\dist (5'b00001), .out(Product_q));
  Adder #(.width(32)) adder_4 (.a(Product_q), .b(32'h1), .out(adder_4_out));  // open: cin, cout

  // Notes on the sheet:
  //   Clock to Registers
  //   contents of rom_1 (hex, n*v repeats v):
  //   6 5 1f 5 1f 5 1f 5 1f 5 1f 5 1f 5 1f 5 1f 5 1f 5 1f 5 1f 5 1f 5 1f 5 1f 5 1f 5 1f 5 1f
endmodule

module _16_bit_Division (
  input  [15:0] Dividend,
  input  [15:0] Divisor,
  input  division_instruction,
  input  Clock,
  output [15:0] Quotient,
  output [15:0] Remainder,
  output division_ready
);

  wire and_1_out, and_2_out, comparator_1_eq, comparator_1_gt, comparator_1_lt, not_3_out, not_4_out,
       or_1_out;
  wire [7:0] counter_1_q, rom_1_data;
  wire [15:0] adder_1_out, adder_2_out, adder_5_out, multiplexer_1_out, multiplexer_2_out, multiplexer_7_out,
       not_1_out, not_2_out, Quotient_q, shifter_4_out;
  wire [31:0] adder_3_out, adder_4_out, bit_extender_1_out, bit_extender_2_out, Divisor_q, multiplexer_3_out,
       multiplexer_4_out, multiplexer_5_out, multiplexer_6_out, multiplexer_8_out, Remainder_q,
       shifter_1_out, shifter_2_out, shifter_3_out, subtractor_1_out, undriven;

  assign not_1_out = ~Dividend;  // NOT_Gate not_1, 16 bits wide
  assign not_2_out = ~Divisor;  // NOT_Gate not_2, 16 bits wide
  Adder #(.width(16)) adder_1 (.a(not_1_out), .b(16'h1), .out(adder_1_out));  // open: cin, cout
  Adder #(.width(16)) adder_2 (.a(not_2_out), .b(16'h1), .out(adder_2_out));  // open: cin, cout
  Multiplexer #(.width(16)) multiplexer_1 (
    .in0(Dividend), .in1(adder_1_out), .out(multiplexer_1_out), .sel(Dividend[15]));  // open: en
  Multiplexer #(.width(16)) multiplexer_2 (
    .in0(Divisor), .in1(adder_2_out), .out(multiplexer_2_out), .sel(Divisor[15]));  // open: en
  assign bit_extender_1_out = {{16{1'b0}}, multiplexer_1_out};  // Bit_Extender bit_extender_1
  assign bit_extender_2_out = {{16{1'b0}}, multiplexer_2_out};  // Bit_Extender bit_extender_2
  Shifter #(.width(32)) shifter_1 (.in(bit_extender_1_out), .\dist (5'b01000), .out(shifter_1_out));
  Shifter #(.width(32)) shifter_2 (.in(bit_extender_2_out), .\dist (5'b10000), .out(shifter_2_out));
  Adder #(.width(32)) adder_3 (.a(undriven), .out(adder_3_out));  // open: b, cin, cout
  Divider #(.width(16)) divider_1 (.a(multiplexer_1_out), .b(multiplexer_2_out), .rem(Remainder));  // open: out, upper
  Counter #(.max('h23), .ongoal("stay"), .trigger("falling")) counter_1 (
    .Q(counter_1_q), .carry(division_ready), .clk(and_1_out), .clr(not_3_out));  // open: load, D, count
  not not_3 (not_3_out, division_instruction);
  and and_1 (and_1_out, division_instruction, Clock);
  Register #(.width(32), .trigger("falling")) u_Remainder (
    .D(multiplexer_3_out), .en(rom_1_data[2]), .Q(Remainder_q), .clk(and_1_out), .clr(not_4_out));
  Multiplexer #(.width(32), .enable("false")) multiplexer_3 (
    .in0(shifter_1_out), .in1(multiplexer_6_out), .out(multiplexer_3_out), .sel(rom_1_data[0]));
  Multiplexer #(.width(32), .enable("false")) multiplexer_4 (
    .in0(shifter_2_out), .in1(multiplexer_8_out), .out(multiplexer_4_out), .sel(rom_1_data[0]));
  ROM rom_1 (.addr(counter_1_q), .data(rom_1_data));  // open: sel
  Register #(.width(32), .trigger("falling")) u_Divisor (
    .D(multiplexer_4_out), .en(rom_1_data[1]), .Q(Divisor_q), .clk(and_1_out), .clr(not_4_out));
  Comparator #(.width(32)) comparator_1 (
    .a(Remainder_q), .b({32{1'b0}}), .gt(comparator_1_gt), .eq(comparator_1_eq), .lt(comparator_1_lt));
  Adder #(.width(32)) adder_4 (.a(Remainder_q), .b(Divisor_q), .out(adder_4_out));  // open: cin, cout
  Subtractor #(.width(32)) subtractor_1 (.a(Remainder_q), .b(Divisor_q), .out(subtractor_1_out));  // open: bin, bout
  not not_4 (not_4_out, division_instruction);
  Multiplexer #(.width(32), .enable("false")) multiplexer_5 (
    .in0(subtractor_1_out), .in1(adder_4_out), .out(multiplexer_5_out), .sel(comparator_1_lt));
  Shifter #(.width(32), .shift("lr")) shifter_3 (.in(Divisor_q), .\dist (5'b00001), .out(shifter_3_out));
  or or_1 (or_1_out, comparator_1_gt, comparator_1_eq);
  and and_2 (and_2_out, or_1_out, rom_1_data[1]);
  Multiplexer #(.width(32), .enable("false")) multiplexer_6 (
    .in0(multiplexer_5_out), .in1(Remainder_q), .out(multiplexer_6_out), .sel(and_2_out));
  Multiplexer #(.width(16), .enable("false")) multiplexer_7 (
    .in0(adder_5_out), .in1(shifter_4_out), .out(multiplexer_7_out), .sel(comparator_1_lt));
  Multiplexer #(.width(32), .enable("false")) multiplexer_8 (
    .in0(Divisor_q), .in1(shifter_3_out), .out(multiplexer_8_out), .sel(rom_1_data[4]));
  Register #(.width(16), .trigger("falling")) u_Quotient (
    .D(multiplexer_7_out), .en(rom_1_data[3]), .Q(Quotient_q), .clk(and_1_out), .clr(not_4_out));
  Shifter #(.width(16)) shifter_4 (.in(Quotient_q), .\dist (4'b0001), .out(shifter_4_out));
  Shifter #(.width(16), .shift("lr")) shifter_5 (.in(Quotient_q), .\dist (4'b1000), .out(Quotient));
  Adder #(.width(16)) adder_5 (.a(shifter_4_out), .b(16'h1), .out(adder_5_out));  // open: cin, cout

  // Notes on the sheet:
  //   contents of rom_1 (hex, n*v repeats v):
  //   6 5 1f 5 1f 5 1f 5 1f 5 1f 5 1f 5 1f 5 1f 5 1f 5 1f 5 1f 5 1f 5 1f 5 1f 5 1f 5 1f 5 1f
  //   Clock for internal registers
endmodule
